# Fritzing sketch Bareboard (saved by Fritzing 0.9.2b)
breadboards: 1

parts:
  U1 = atmega328 [package=dip]
  XTAL1 = Crystal [frequency="16 Mhz" package=THT]
  C1 = Ceramic Capacitor [capacitance=100nF package="100 mil [THT, multilayer]"]
  C2 = Ceramic Capacitor [capacitance=100nF package="100 mil [THT, multilayer]"]
  R1 = Resistor [tolerance=±5% resistance=10k package=THT]
  LED1 = LED - 5mm [color="Red (633nm)" package="5 mm [THT]"]
  R2 = Resistor [tolerance=±5% resistance=220 package=THT]
  R3 = Resistor [tolerance=±5% resistance=10k package=THT]
  S1 = Pushbutton [package="[THT]"]
  Q1 = Basic FET N-Channel [package="TO220 [THT]"]
  VCC1 = 4 x AAA Battery Mount

nets:
  N1: U1.RESET, R1.Pin_1
  N2: U1.VCC, R1.Pin_0, S1.Pin_3, S1.Pin_4, VCC1.+
  N3: U1.GND#7, C1.0, C2.0
  N4: U1.XLAT1, XTAL1.pin_0, C1.1
  N5: U1.XLAT2, XTAL1.pin_1, C2.1
  N6: U1.D12, R3.Pin_0, S1.Pin_1, S1.Pin_2, Q1.gate
  N7: U1.D13, LED1.cathode
  N8: U1.GND#21, R2.Pin_0, R3.Pin_1, Q1.drain
  N9: LED1.anode, R2.Pin_1
  N10: Q1.source, VCC1.-
