# Fritzing sketch Regular_Arduino (saved by Fritzing 0.9.2b)
breadboards: 1

parts:
  R3 = Resistor [tolerance=±5% resistance=10k package=THT]
  S1 = Pushbutton [package="[THT]"]
  Q1 = Basic FET N-Channel [package="TO220 [THT]"]
  Part1 = Arduino Nano (Rev3.0)
  VCC1 = 4 x AAA Battery Mount

nets:
  N1: R3.Pin_0, S1.Pin_1, S1.Pin_2, Q1.gate, Part1.D12/MISO
  N2: R3.Pin_1, Q1.drain, Part1.GND
  N3: S1.Pin_3, S1.Pin_4, Part1.VIN, VCC1.+
  N4: Q1.source, VCC1.-
